// Digital circuit DWAK2.dig as structural Verilog
module DWAK2 (
  input  Program_clock,
  input  [63:0] in_2,
  output [63:0] out_3
);

  wire arithm_1_act, arithm_1_ram_store, arithm_1_reg_store1, comparator_1_eq, DONE_eq, fetcher_1_act,
       fetcher_1_write_store, instruction_memory_1_p3, instruction_memory_1_p8, instruction_memory_1_p9,
       instruction_memory_1_p10, instruction_memory_1_p11, instruction_memory_1_p12, mov_1_act,
       mov_1_ram_store, mov_1_reg_store, multiplexer_1_out, multiplexer_2_out, not_1_out, register_1_q,
       rgrm_merger_1_gr_5, rgrm_merger_1_mr_5, rgrm_merger_2_gr_5, rgrm_merger_2_mr_5, rgrm_merger_3_p13,
       rgrm_merger_3_p23, rgrm_merger_4_gr_5, rgrm_merger_4_mr_5;
  wire [1:0] arithm_1_mode_out, fetcher_1_mode_out, mode_merger_1_mode, mode_merger_2_mode,
       mode_merger_3_mode, mode_register_1_mode, mov_1_mode_out;
  wire [2:0] instruction_memory_1_p1;
  wire [7:0] arithm_1_reg_read1, arithm_1_reg_read2, arithm_1_reg_write1, fetcher_1_reg_read1,
       fetcher_1_write_reg, mov_1_reg_read1, mov_1_reg_read2, mov_1_reg_write, rgrm_merger_1_gr_1,
       rgrm_merger_1_gr_2, rgrm_merger_1_gr_3, rgrm_merger_2_gr_1, rgrm_merger_2_gr_2, rgrm_merger_2_gr_3,
       rgrm_merger_3_p27, rgrm_merger_3_p29, rgrm_merger_3_p31, rgrm_merger_4_gr_1, rgrm_merger_4_gr_2,
       rgrm_merger_4_gr_3;
  wire [9:0] counter_1_out;
  wire [63:0] arithm_1_ram_data, arithm_1_ram_read1, arithm_1_ram_read2, arithm_1_ram_write,
       arithm_1_reg_data1, fetcher_1_ram_addr1, fetcher_1_write_data, instruction_memory_1_p2,
       instruction_memory_1_p5, instruction_memory_1_p6, instruction_memory_1_p7, mov_1_ram_data,
       mov_1_ram_read1, mov_1_ram_read2, mov_1_ram_write, mov_1_reg_data, Program_ROM_d, ram_1_res_read1,
       registers_1_res_read1, registers_1_res_read2, rgrm_merger_1_gr_4, rgrm_merger_1_mr_1,
       rgrm_merger_1_mr_2, rgrm_merger_1_mr_3, rgrm_merger_1_mr_4, rgrm_merger_2_gr_4, rgrm_merger_2_mr_1,
       rgrm_merger_2_mr_2, rgrm_merger_2_mr_3, rgrm_merger_2_mr_4, rgrm_merger_3_p15, rgrm_merger_3_p17,
       rgrm_merger_3_p19, rgrm_merger_3_p21, rgrm_merger_3_p25, rgrm_merger_4_gr_4, rgrm_merger_4_mr_1,
       rgrm_merger_4_mr_3, rgrm_merger_4_mr_4;

  Button button_1 ();  // open: out
  Multiplexer multiplexer_1 (.sel(DONE_eq), .in_0(Program_clock), .in_1(1'b0), .out(multiplexer_1_out));
  mode_merger mode_merger_1 (.mode_1(2'b10), .mode_2(arithm_1_mode_out), .mode(mode_merger_1_mode));
  mode_merger mode_merger_2 (.mode_1(mode_merger_1_mode), .mode_2(mov_1_mode_out), .mode(mode_merger_2_mode));
  mode_merger mode_merger_3 (.mode_1(mode_merger_2_mode), .mode_2(fetcher_1_mode_out), .mode(mode_merger_3_mode));
  Multiplexer multiplexer_2 (
    .sel(register_1_q), .in_0(Program_clock), .in_1(multiplexer_1_out), .out(multiplexer_2_out));
  mode_register mode_register_1 (.clock(multiplexer_1_out), .in(mode_merger_3_mode), .mode(mode_register_1_mode));
  EEPROMDualPort #(.AddrBits(10), .isProgramMemory("true"), .Bits(64)) Program_ROM (
    .A(counter_1_out), .Din({64{1'b0}}), .str(1'b0), .C(multiplexer_2_out), .ld(1'b1), .D(Program_ROM_d));
  // instruction_memory instruction_memory_1: pin names not known; wires that end beside it: instruction_memory_1_p1, instruction_memory_1_p2, instruction_memory_1_p3, multiplexer_1_out, instruction_memory_1_p5, instruction_memory_1_p6, instruction_memory_1_p7, instruction_memory_1_p8, instruction_memory_1_p9, instruction_memory_1_p10, instruction_memory_1_p11, instruction_memory_1_p12
  fetcher fetcher_1 (
    .mode(mode_register_1_mode), .IP(registers_1_res_read1), .word1(ram_1_res_read1), .word(ram_1_res_read1),
    .clock(multiplexer_1_out), .act(fetcher_1_act), .reg_read1(fetcher_1_reg_read1),
    .ram_addr1(fetcher_1_ram_addr1), .im_addr(instruction_memory_1_p1), .im_word(instruction_memory_1_p2),
    .im_store(instruction_memory_1_p3), .write_reg(fetcher_1_write_reg), .write_data(fetcher_1_write_data),
    .write_store(fetcher_1_write_store), .mode_out(fetcher_1_mode_out));
  Counter #(.Bits(10)) counter_1 (.en(1'b1), .C(multiplexer_2_out), .clr(1'b0), .out(counter_1_out));  // open: ovf
  Comparator #(.Bits(10)) comparator_1 (.a(counter_1_out), .b({10{1'b1}}), .eq(comparator_1_eq));  // open: gt, lt
  Register register_1 (.D(1'b1), .C(comparator_1_eq), .en(not_1_out), .Q(register_1_q));
  not not_1 (not_1_out, register_1_q);
  ARITHM arithm_1 (
    .word1(instruction_memory_1_p5), .word2(instruction_memory_1_p6), .word3(instruction_memory_1_p7),
    .reg_in1(registers_1_res_read1), .reg_in2(registers_1_res_read2), .ram_in1(ram_1_res_read1),
    .mode(mode_register_1_mode), .act(arithm_1_act), .reg_read1(arithm_1_reg_read1),
    .reg_read2(arithm_1_reg_read2), .reg_write1(arithm_1_reg_write1), .reg_data1(arithm_1_reg_data1),
    .reg_store1(arithm_1_reg_store1), .RAM_read1(arithm_1_ram_read1), .RAM_read2(arithm_1_ram_read2),
    .RAM_write(arithm_1_ram_write), .RAM_data(arithm_1_ram_data), .RAM_store(arithm_1_ram_store),
    .mode_out(arithm_1_mode_out));
  MOV mov_1 (
    .word1(instruction_memory_1_p5), .word2(instruction_memory_1_p6), .word3(instruction_memory_1_p7),
    .reg_in1(registers_1_res_read1), .reg_in2(registers_1_res_read2), .ram_in1(ram_1_res_read1),
    .mode(mode_register_1_mode), .act(mov_1_act), .reg_read1(mov_1_reg_read1), .reg_read2(mov_1_reg_read2),
    .reg_write(mov_1_reg_write), .reg_data(mov_1_reg_data), .reg_store(mov_1_reg_store),
    .RAM_read1(mov_1_ram_read1), .RAM_read2(mov_1_ram_read2), .RAM_write(mov_1_ram_write),
    .RAM_data(mov_1_ram_data), .RAM_store(mov_1_ram_store), .mode_out(mov_1_mode_out));
  Comparator #(.Bits(64)) DONE (.a(instruction_memory_1_p5), .b(64'h7f9), .eq(DONE_eq));  // open: gt, lt
  rgrm_merger rgrm_merger_1 (
    .rm_5(1'b0), .rm_4({64{1'b0}}), .rm_3({64{1'b0}}), .rm_2({64{1'b0}}), .rm_1({64{1'b0}}), .rg_5(1'b0),
    .rg_4({64{1'b0}}), .rg_3({8{1'b0}}), .rg_2({8{1'b0}}), .rg_1({8{1'b0}}), .dir(arithm_1_act),
    .RG_1_2(arithm_1_reg_read1), .RG_2_2(arithm_1_reg_read2), .RG_3_2(arithm_1_reg_write1),
    .RG_4_2(arithm_1_reg_data1), .RG_5_2(arithm_1_reg_store1), .RM_1_2(arithm_1_ram_read1),
    .RM_2_2(arithm_1_ram_read2), .RM_3_2(arithm_1_ram_write), .RM_4_2(arithm_1_ram_data),
    .RM_5_2(arithm_1_ram_store), .mr_5(rgrm_merger_1_mr_5), .mr_4(rgrm_merger_1_mr_4),
    .mr_3(rgrm_merger_1_mr_3), .mr_2(rgrm_merger_1_mr_2), .mr_1(rgrm_merger_1_mr_1),
    .gr_5(rgrm_merger_1_gr_5), .gr_4(rgrm_merger_1_gr_4), .gr_3(rgrm_merger_1_gr_3),
    .gr_2(rgrm_merger_1_gr_2), .gr_1(rgrm_merger_1_gr_1));
  rgrm_merger rgrm_merger_2 (
    .rm_5(rgrm_merger_1_mr_5), .rm_4(rgrm_merger_1_mr_4), .rm_3(rgrm_merger_1_mr_3),
    .rm_2(rgrm_merger_1_mr_2), .rm_1(rgrm_merger_1_mr_1), .rg_5(rgrm_merger_1_gr_5),
    .rg_4(rgrm_merger_1_gr_4), .rg_3(rgrm_merger_1_gr_3), .rg_2(rgrm_merger_1_gr_2),
    .rg_1(rgrm_merger_1_gr_1), .dir(mov_1_act), .RG_1_2(mov_1_reg_read1), .RG_2_2(mov_1_reg_read2),
    .RG_3_2(mov_1_reg_write), .RG_4_2(mov_1_reg_data), .RG_5_2(mov_1_reg_store), .RM_1_2(mov_1_ram_read1),
    .RM_2_2(mov_1_ram_read2), .RM_3_2(mov_1_ram_write), .RM_4_2(mov_1_ram_data), .RM_5_2(mov_1_ram_store),
    .mr_5(rgrm_merger_2_mr_5), .mr_4(rgrm_merger_2_mr_4), .mr_3(rgrm_merger_2_mr_3),
    .mr_2(rgrm_merger_2_mr_2), .mr_1(rgrm_merger_2_mr_1), .gr_5(rgrm_merger_2_gr_5),
    .gr_4(rgrm_merger_2_gr_4), .gr_3(rgrm_merger_2_gr_3), .gr_2(rgrm_merger_2_gr_2), .gr_1(rgrm_merger_2_gr_1));
  // rgrm_merger rgrm_merger_3: pin names not known; wires that end beside it: fetcher_1_act, fetcher_1_reg_read1, {8{1'b0}}, fetcher_1_write_reg, fetcher_1_write_data, fetcher_1_write_store, fetcher_1_ram_addr1, {64{1'b0}}, {64{1'b0}}, {64{1'b0}}, 1'b0, rgrm_merger_2_mr_5, rgrm_merger_3_p13, rgrm_merger_2_mr_4, rgrm_merger_3_p15, rgrm_merger_2_mr_3, rgrm_merger_3_p17, rgrm_merger_2_mr_2, rgrm_merger_3_p19, rgrm_merger_2_mr_1, rgrm_merger_3_p21, rgrm_merger_2_gr_5, rgrm_merger_3_p23, rgrm_merger_2_gr_4, rgrm_merger_3_p25, rgrm_merger_2_gr_3, rgrm_merger_3_p27, rgrm_merger_2_gr_2, rgrm_merger_3_p29, rgrm_merger_2_gr_1, rgrm_merger_3_p31
  rgrm_merger rgrm_merger_4 (
    .rm_5(rgrm_merger_3_p13), .rm_4(rgrm_merger_3_p15), .rm_3(rgrm_merger_3_p17), .rm_2(rgrm_merger_3_p19),
    .rm_1(rgrm_merger_3_p21), .rg_5(rgrm_merger_3_p23), .rg_4(rgrm_merger_3_p25), .rg_3(rgrm_merger_3_p27),
    .rg_2(rgrm_merger_3_p29), .rg_1(rgrm_merger_3_p31), .dir(not_1_out), .RG_1_2({8{1'b0}}),
    .RG_2_2({8{1'b0}}), .RG_3_2({8{1'b0}}), .RG_4_2({64{1'b0}}), .RG_5_2(1'b0), .RM_1_2({64{1'b0}}),
    .RM_2_2({64{1'b0}}), .RM_3_2({{54{1'b0}}, counter_1_out}), .RM_4_2(Program_ROM_d), .RM_5_2(not_1_out),
    .mr_5(rgrm_merger_4_mr_5), .mr_4(rgrm_merger_4_mr_4), .mr_3(rgrm_merger_4_mr_3),
    .mr_1(rgrm_merger_4_mr_1), .gr_5(rgrm_merger_4_gr_5), .gr_4(rgrm_merger_4_gr_4),
    .gr_3(rgrm_merger_4_gr_3), .gr_2(rgrm_merger_4_gr_2), .gr_1(rgrm_merger_4_gr_1));  // open: mr_2
  ram ram_1 (
    .addr_read1(rgrm_merger_4_mr_1), .addr_read2(in_2), .addr_write(rgrm_merger_4_mr_3),
    .data_write(rgrm_merger_4_mr_4), .store_write(rgrm_merger_4_mr_5), .clock(multiplexer_2_out),
    .res_read1(ram_1_res_read1), .res_read2(out_3));
  registers registers_1 (
    .reg_read1(rgrm_merger_4_gr_1), .reg_read2(rgrm_merger_4_gr_2), .reg_write(rgrm_merger_4_gr_3),
    .data_write(rgrm_merger_4_gr_4), .store_write(rgrm_merger_4_gr_5), .clock(multiplexer_2_out),
    .res_read1(registers_1_res_read1), .res_read2(registers_1_res_read2));

  // Notes on the sheet:
  //   Program_clock: Hz: 2147483647
  //   in_2: default 65535
  //   contents of Program_ROM (hex, n*v repeats v):
  //   23,ffff,f,a,2,506a,ffff,7f9
endmodule
